# Fritzing sketch circuit (saved by Fritzing 0.9.3b)
breadboards: 1

parts:
  LCD1 = LCD screen
  元件1 = Arduino Uno (Rev3)
  S1 = Pushbutton [package="[THT]"]
  R1 = Resistor [tolerance=±5% resistance=10k package=THT]
  R2 = Photocell (LDR) [package=THT]
  R3 = Resistor [tolerance=±5% resistance=330 package=THT]
  R4 = Rotary Potentiometer (Small) [maximum_resistance=10kΩ package=THT]

nets:
  VSS: LCD1.VSS, LCD1.LED+, LCD1.LED-, 元件1.GND, R1.Pin_1, R3.Pin_1, R4.leg2
  VDD: LCD1.VDD, LCD1.R/W, 元件1.5V, S1.Pin_3, S1.Pin_4, R2.pin_0, R4.leg1
  N1: LCD1.V0, R4.wiper
  N2: LCD1.RS, 元件1.D13/SCK
  N3: LCD1.E, 元件1.D12/MISO
  N4: LCD1.DB4, 元件1.D11_PWM/MOSI
  N5: LCD1.DB5, 元件1.D10_PWM/SS
  N6: LCD1.DB6, 元件1.D9_PWM
  N7: LCD1.DB7, 元件1.D8
  N8: 元件1.A0, R2.pin_1, R3.Pin_0
  N9: 元件1.D7, S1.Pin_1, S1.Pin_2, R1.Pin_0
